# Fritzing sketch Circuit _Diagram (saved by Fritzing 0.9.3b)

parts:
  L298N2 = L298N DC motor driver
  hc-sr2 = hc-sr04
  Part3 = Arduino Uno (Rev3)
  VCC2 = Battery block 9V
  M2 = DC Motor
  M3 = DC Motor

nets:
  N1: L298N2.OUT1, M2.pin_2
  N2: L298N2.OUT2, M2.pin_1
  N3: L298N2.OUT3, M3.pin_2
  N4: L298N2.OUT4, M3.pin_1
  N5: L298N2.IN1, Part3.D7
  N6: L298N2.IN2, Part3.D6_PWM
  N7: L298N2.IN3, Part3.D5_PWM
  N8: L298N2.IN4, Part3.D4
  N9: hc-sr2.Trig, Part3.D13/SCK
  N10: hc-sr2.Echo, Part3.D12/MISO
  N11: Part3.5V, VCC2.+
  N12: Part3.GND, VCC2.-

custom parts:
  L298N DC motor driver: 2x DC motor driver with 78M05 positive voltage regulator (7..35 V) L298N: max 46 V, 2 A Set 5 V Enable jumper to enable 5 V regultor (needed for the L298N) and +5 V output at screw terminal or supply external +5 V at screw terminal Set ENA and/or ENB to +5 V to enable motor permanently or supply ENA and/or ENB with PWM signal IN1 and IN2 set rotation directory for motor A (OUT1/OUT2) IN2 and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
